// Logisim project ALU design.circ as structural Verilog: 1 circuit, main circuit main
module main (
  input  CS2,
  input  [3:0] A,
  input  CS1,
  input  CS0,
  input  [3:0] B,
  output Cout,
  output S4,
  output S3,
  output S2,
  output S1
);

  wire n7404_1_p3, n7404_1_p5, n7404_1_p8, n7404_1_p9, n7404_1_p10, n7404_1_p11, n7404_2_p2, n7404_2_p4,
       n7408_1_p3, n7408_1_p8, n7483_1_p4, n7483_1_p7, n7483_1_p9, n7483_1_p14, n7486_1_p6, n7486_1_p14;

  // _7404 7404_1: pin names not known; wires that end beside it: CS0, CS2, n7404_1_p3, CS1, n7404_1_p5, 1'b0, 1'b1, n7404_1_p8, n7404_1_p9, n7404_1_p10, n7404_1_p11
  // _7486 7486_1: pin names not known; wires that end beside it: CS1, B[0], n7404_1_p10, CS1, B[1], n7486_1_p6, 1'b0, 1'b1, CS1, B[3], n7404_1_p8, CS1, B[2], n7486_1_p14
  // _7408 7408_1: pin names not known; wires that end beside it: CS1, n7404_1_p3, n7408_1_p3, 1'b0, 1'b1, CS2, n7404_1_p5, n7408_1_p8
  // _7483 7483_1: pin names not known; wires that end beside it: A[3], S3, A[2], n7483_1_p4, 1'b1, S2, n7483_1_p7, A[1], n7483_1_p9, S4, Cout, n7408_1_p8, 1'b0, n7483_1_p14, A[0], S1
  // _7404 7404_2: pin names not known; wires that end beside it: n7486_1_p14, n7404_2_p2, n7486_1_p6, n7404_2_p4, 1'b0, 1'b1
  // _7432 7432_1: pin names not known; wires that end beside it: n7408_1_p3, n7404_1_p11, n7483_1_p14, n7408_1_p3, n7404_1_p9, n7483_1_p9, 1'b0, 1'b1, n7408_1_p3, n7404_2_p2, n7483_1_p4, n7408_1_p3, n7404_2_p4, n7483_1_p7

  // Notes on the sheet:
  //   CS2'
  //   CS1'
  //   NOT Gate
  //   B1
  //   B2
  //   XOR Gate
  //   B3
  //   B4
  //   A4
  //   A3
  //   A2
  //   Adder
  //   AND Gate
  //   A1
  //   CS1' CS2
  //   CS2' CS1
  //   D1
  //   D4
  //   NOT Gate
  //   Y1
  //   D2
  //   Y4
  //   OR Gate
  //   D3
  //   Y3
  //   Y2
endmodule
