// Logisim project Alu Final.circ as structural Verilog: 1 circuit, main circuit main
module main (
  input  CS2,
  input  [3:0] A,
  input  CS1,
  input  CS0,
  input  [3:0] B,
  output out_6,
  output F1,
  output F2,
  output F3,
  output F4,
  output C,
  output out_12,
  output out_13,
  output out_14,
  output out_15,
  output Sign,
  output Zero,
  output Overflow
);

  wire n7404_1_pin2, n7404_1_pin4, n7404_1_pin10, n7404_1_pin11, n7404_1_pin12, n7404_1_pin13, n7404_2_pin2,
       n7404_2_pin4, n7404_2_pin6, n7404_2_pin8, n7404_2_pin10, n7404_2_pin12, n7404_3_pin2, n7404_3_pin4,
       n7404_3_pin6, n7404_3_pin8, n7408_1_pin3, n7408_1_pin11, n7408_2_pin3, n7408_2_pin6, n7486_1_pin6,
       n7486_1_pin8, n7486_2_pin3, n7486_2_pin6, n7486_2_pin8, n7486_2_pin11, n7486_3_pin3, n7486_3_pin6,
       n74157_1_pin4, n74157_1_pin7, n74157_1_pin9, n74157_1_pin12, n74283_1_pin2, n74283_1_pin6,
       n74283_1_pin11, n74283_1_pin15;

  _7404 u_7404_1 (
    .pin1(CS2), .pin2(n7404_1_pin2), .pin3(CS1), .pin4(n7404_1_pin4), .pin13(n7404_1_pin13),
    .pin12(n7404_1_pin12), .pin11(n7404_1_pin11), .pin10(n7404_1_pin10));  // open: pin5, pin6, pin9, pin8
  _7486 u_7486_1 (
    .pin1(CS1), .pin2(B[0]), .pin3(n7404_1_pin11), .pin4(CS1), .pin5(B[1]), .pin6(n7486_1_pin6), .pin13(CS1),
    .pin12(B[3]), .pin11(n7404_1_pin13), .pin10(CS1), .pin9(B[2]), .pin8(n7486_1_pin8));
  _7408 u_7408_1 (
    .pin1(CS1), .pin2(n7404_1_pin2), .pin3(n7408_1_pin3), .pin13(CS2), .pin12(n7404_1_pin4),
    .pin11(n7408_1_pin11));  // open: pin4, pin5, pin6, pin10, pin9, pin8
  _74283 u_74283_1 (
    .pin1(out_13), .pin2(n74283_1_pin2), .pin3(A[1]), .pin4(out_12), .pin5(A[0]), .pin6(n74283_1_pin6),
    .pin7(n7408_1_pin11), .pin15(n74283_1_pin15), .pin14(A[2]), .pin13(out_14), .pin12(A[3]),
    .pin11(n74283_1_pin11), .pin10(out_15), .pin9(C));
  _7404 u_7404_2 (
    .pin1(n7486_1_pin8), .pin2(n7404_2_pin2), .pin3(n7486_1_pin6), .pin4(n7404_2_pin4), .pin5(A[0]),
    .pin6(n7404_2_pin6), .pin13(A[1]), .pin12(n7404_2_pin12), .pin11(A[2]), .pin10(n7404_2_pin10),
    .pin9(A[3]), .pin8(n7404_2_pin8));
  _7432 u_7432_1 (
    .pin1(n7408_1_pin3), .pin2(n7404_1_pin10), .pin3(n74283_1_pin6), .pin4(n7408_1_pin3),
    .pin5(n7404_1_pin12), .pin6(n74283_1_pin11), .pin13(n7408_1_pin3), .pin12(n7404_2_pin2),
    .pin11(n74283_1_pin15), .pin10(n7408_1_pin3), .pin9(n7404_2_pin4), .pin8(n74283_1_pin2));
  _7486 u_7486_2 (
    .pin1(A[0]), .pin2(B[3]), .pin3(n7486_2_pin3), .pin4(A[1]), .pin5(B[2]), .pin6(n7486_2_pin6),
    .pin13(B[1]), .pin12(A[2]), .pin11(n7486_2_pin11), .pin10(B[0]), .pin9(A[3]), .pin8(n7486_2_pin8));
  _74157 u_74157_1 (
    .pin1(n7404_1_pin4), .pin2(n7404_2_pin6), .pin3(n7486_2_pin3), .pin4(n74157_1_pin4),
    .pin5(n7404_2_pin12), .pin6(n7486_2_pin6), .pin7(n74157_1_pin7), .pin14(n7404_2_pin8),
    .pin13(n7486_2_pin8), .pin12(n74157_1_pin12), .pin11(n7404_2_pin10), .pin10(n7486_2_pin11),
    .pin9(n74157_1_pin9));  // open: pin15
  _7486 u_7486_3 (
    .pin1(C), .pin2(out_15), .pin3(n7486_3_pin3), .pin4(n74283_1_pin11), .pin5(A[3]), .pin6(n7486_3_pin6),
    .pin13(n7486_3_pin3), .pin12(n7486_3_pin6), .pin11(Overflow));  // open: pin10, pin9, pin8
  _74157 u_74157_2 (
    .pin1(CS0), .pin2(n74157_1_pin4), .pin3(out_12), .pin4(F1), .pin5(n74157_1_pin7), .pin6(out_13),
    .pin7(F2), .pin14(n74157_1_pin12), .pin13(out_15), .pin12(F4), .pin11(n74157_1_pin9), .pin10(out_14),
    .pin9(F3));  // open: pin15
  _7404 u_7404_3 (
    .pin1(F1), .pin2(n7404_3_pin2), .pin3(F2), .pin4(n7404_3_pin4), .pin5(F4), .pin6(n7404_3_pin6),
    .pin9(F3), .pin8(n7404_3_pin8));  // open: pin13, pin12, pin11, pin10
  _7408 u_7408_2 (
    .pin1(n7404_3_pin2), .pin2(n7404_3_pin4), .pin3(n7408_2_pin3), .pin4(n7404_3_pin8), .pin5(n7404_3_pin6),
    .pin6(n7408_2_pin6), .pin13(n7408_2_pin3), .pin12(n7408_2_pin6), .pin11(Zero));  // open: pin10, pin9, pin8

  assign out_6 = C;
  assign Sign = F4;

  // Notes on the sheet:
  //   A4
  //   A3
  //   A2
  //   A1
  //   CS2'
  //   CS1'
  //   NOT Gate
  //   B1
  //   B2
  //   B4
  //   XOR Gate
  //   B3
  //   B2
  //   B3
  //   B1
  //   A2
  //   A1
  //   B4
  //   A4
  //   A3
  //   AND Gate
  //   Adder
  //   CS1' CS2
  //   D1
  //   D4
  //   Y4
  //   CS2' CS1
  //   D2
  //   A1'
  //   Y1
  //   NOT Gate
  //   OR Gate
  //   D3
  //   Y3
  //   Y2
  //   A2'
  //   Cout
  //   S4
  //   S3
  //   S2
  //   S1
  //   A3'
  //   A4'
  //   xor1
  //   xor2
  //   XOR Gate
  //   xor4
  //   xor3
  //   L2
  //   L1
  //   S4
  //   Y4
  //   A4
  //   MUX
  //   Cout
  //   L4
  //   XOR
  //   L3
  //   NOT Gate
  //   AND Gate
endmodule
