// Logisim project practice1.circ as structural Verilog: 1 circuit, main circuit Circuit 1
module Circuit_1 (
  input  A,
  input  B,
  output F
);

  wire and_1_out, and_2_out, not_1_out, not_2_out;

  not not_1 (not_1_out, A);
  not not_2 (not_2_out, B);
  // _7404 7404_1: pin names not known
  and and_1 (and_1_out, not_1_out, B);
  and and_2 (and_2_out, A, not_2_out);
  or or_1 (F, and_1_out, and_2_out);

  // Notes on the sheet:
  //   F= A'B + AB'
endmodule
